// Logisim project 8-bit Datapath.circ as structural Verilog: 4 circuits, main circuit main
module main (
  input  in_1,
  output [3:0] out_2,
  output [3:0] out_3,
  output [3:0] out_4,
  output [7:0] out_5,
  output out_6,
  output [7:0] out_7,
  output [2:0] out_8
);

  wire clock_1_out;
  wire [3:0] adder_1_out, register_1_q;
  wire [7:0] n8_bit_register_1_out_7, n8_bit_register_1_out_8;
  wire [15:15] rom_1_data;

  Register #(.width(4)) register_1 (.D(adder_1_out), .Q(register_1_q), .clk(clock_1_out));  // open: en, clr
  Adder #(.width(4)) adder_1 (.a(register_1_q), .b(4'b0001), .out(adder_1_out));  // open: cin, cout
  ROM #(.addrWidth(4), .dataWidth(16)) rom_1 (
    .addr(register_1_q), .data({rom_1_data[15], out_8, out_4, out_3, out_2}));  // open: sel
  _8_bit_Register u_8_bit_register_1 (
    .Reg_Write(rom_1_data[15]), .Clock(clock_1_out), .out_7(n8_bit_register_1_out_7), .in_3(out_4),
    .out_8(n8_bit_register_1_out_8), .Read_Register_2(out_3), .in_5(out_5), .in_6(out_2));
  Clock clock_1 (.out(clock_1_out));
  _8_bit_ALU u_8_bit_alu_1 (
    .A(n8_bit_register_1_out_7), .B(n8_bit_register_1_out_8), .out_5(out_5), .Cout(out_6), .Cin(in_1),
    .Opcode(out_8));

  assign out_7 = out_5;

  // Notes on the sheet:
  //   contents of rom_1 (hex, n*v repeats v):
  //   9021 a354 c140 8687 d097
endmodule

module _8_bit_Register (
  input  Reg_Write,
  input  Clock,
  input  [3:0] in_3,
  input  [3:0] Read_Register_2,
  input  [7:0] in_5,
  input  [3:0] in_6,
  output [7:0] out_7,
  output [7:0] out_8
);

  wire and_1_out, decoder_1_out0, decoder_1_out1, decoder_1_out2, decoder_1_out3, decoder_1_out4,
       decoder_1_out5, decoder_1_out6, decoder_1_out7, decoder_1_out8, decoder_1_out9;
  wire [7:0] demultiplexer_1_out0, demultiplexer_1_out1, demultiplexer_1_out2, demultiplexer_1_out3,
       demultiplexer_1_out4, demultiplexer_1_out5, demultiplexer_1_out6, demultiplexer_1_out7,
       demultiplexer_1_out8, demultiplexer_1_out9, register_1_q, register_2_q, register_3_q, register_4_q,
       register_5_q, register_6_q, register_7_q, register_8_q, register_9_q, register_10_q;

  Decoder #(.select(4)) decoder_1 (
    .out0(decoder_1_out0), .out1(decoder_1_out1), .out2(decoder_1_out2), .out3(decoder_1_out3),
    .out4(decoder_1_out4), .out5(decoder_1_out5), .out6(decoder_1_out6), .out7(decoder_1_out7),
    .out8(decoder_1_out8), .out9(decoder_1_out9), .sel(in_6));  // open: out10, out11, out12, out13, out14, out15, en
  Demultiplexer #(.select(4), .width(8)) demultiplexer_1 (
    .out0(demultiplexer_1_out0), .out1(demultiplexer_1_out1), .out2(demultiplexer_1_out2),
    .out3(demultiplexer_1_out3), .out4(demultiplexer_1_out4), .out5(demultiplexer_1_out5),
    .out6(demultiplexer_1_out6), .out7(demultiplexer_1_out7), .out8(demultiplexer_1_out8),
    .out9(demultiplexer_1_out9), .in(in_5), .sel(in_6));  // open: out10, out11, out12, out13, out14, out15, en
  and and_1 (and_1_out, Reg_Write, Clock);
  Register register_1 (.D(demultiplexer_1_out0), .en(decoder_1_out0), .Q(register_1_q), .clk(and_1_out));  // open: clr
  Register register_2 (.D(demultiplexer_1_out1), .en(decoder_1_out1), .Q(register_2_q), .clk(and_1_out));  // open: clr
  Register register_3 (.D(demultiplexer_1_out2), .en(decoder_1_out2), .Q(register_3_q), .clk(and_1_out));  // open: clr
  Register register_4 (.D(demultiplexer_1_out3), .en(decoder_1_out3), .Q(register_4_q), .clk(and_1_out));  // open: clr
  Register register_5 (.D(demultiplexer_1_out4), .en(decoder_1_out4), .Q(register_5_q), .clk(and_1_out));  // open: clr
  Register register_6 (.D(demultiplexer_1_out5), .en(decoder_1_out5), .Q(register_6_q), .clk(and_1_out));  // open: clr
  Register register_7 (.D(demultiplexer_1_out6), .en(decoder_1_out6), .Q(register_7_q), .clk(and_1_out));  // open: clr
  Register register_8 (.D(demultiplexer_1_out7), .en(decoder_1_out7), .Q(register_8_q), .clk(and_1_out));  // open: clr
  Register register_9 (.D(demultiplexer_1_out8), .en(decoder_1_out8), .Q(register_9_q), .clk(and_1_out));  // open: clr
  Register register_10 (
    .D(demultiplexer_1_out9), .en(decoder_1_out9), .Q(register_10_q), .clk(and_1_out));  // open: clr
  Multiplexer #(.select(4), .width(8)) multiplexer_1 (
    .in0(register_1_q), .in1(register_2_q), .in2(register_3_q), .in3(register_4_q), .in4(register_5_q),
    .in5(register_6_q), .in6(register_7_q), .in7(register_8_q), .in8(register_9_q), .in9(register_10_q),
    .out(out_7), .sel(in_3));  // open: in10, in11, in12, in13, in14, in15, en
  Multiplexer #(.select(4), .width(8)) multiplexer_2 (
    .in0(register_1_q), .in1(register_2_q), .in2(register_3_q), .in3(register_4_q), .in4(register_5_q),
    .in5(register_6_q), .in6(register_7_q), .in7(register_8_q), .in8(register_9_q), .in9(register_10_q),
    .out(out_8), .sel(Read_Register_2));  // open: in10, in11, in12, in13, in14, in15, en

  // Notes on the sheet:
  //   Register Selection
  //   Write Data
  //   Read Register 1
  //   Read Data 1
  //   Read Data 2
endmodule

module _1_bit_ALU (
  input  Cin,
  input  A,
  input  B,
  input  [2:0] in_4,
  output Output,
  output Cout
);

  wire adder_1_cout, adder_1_out, and_1_out, not_1_out, or_1_out, subtractor_1_bout, subtractor_1_out,
       xor_1_out;

  and and_1 (and_1_out, A, B);
  or or_1 (or_1_out, A, B);
  xor xor_1 (xor_1_out, A, B);
  not not_1 (not_1_out, A);
  Adder #(.width(1)) adder_1 (.a(A), .b(B), .out(adder_1_out), .cin(Cin), .cout(adder_1_cout));
  Subtractor #(.width(1)) subtractor_1 (.a(A), .b(B), .out(subtractor_1_out), .bin(Cin), .bout(subtractor_1_bout));
  Multiplexer multiplexer_1 (.in0(adder_1_cout), .in1(subtractor_1_bout), .out(Cout), .sel(in_4[0]), .en(in_4[2]));
  Multiplexer #(.select(3)) multiplexer_2 (
    .in0(and_1_out), .in1(or_1_out), .in2(xor_1_out), .in3(not_1_out), .in4(adder_1_out),
    .in5(subtractor_1_out), .out(Output), .sel(in_4));  // open: in6, in7, en

  // Notes on the sheet:
  //   Opcode
endmodule

module _8_bit_ALU (
  input  Cin,
  input  [2:0] Opcode,
  input  [7:0] A,
  input  [7:0] B,
  output [7:0] out_5,
  output Cout
);

  wire n1_bit_alu_1_cout, n1_bit_alu_2_cout, n1_bit_alu_3_cout, n1_bit_alu_4_cout, n1_bit_alu_5_cout,
       n1_bit_alu_6_cout, n1_bit_alu_7_cout;

  _1_bit_ALU u_1_bit_alu_1 (.Cin(Cin), .A(A[0]), .B(B[0]), .Output(out_5[0]), .Cout(n1_bit_alu_1_cout), .in_4(Opcode));
  _1_bit_ALU u_1_bit_alu_2 (
    .Cin(n1_bit_alu_1_cout), .A(A[1]), .B(B[1]), .Output(out_5[1]), .Cout(n1_bit_alu_2_cout), .in_4(Opcode));
  _1_bit_ALU u_1_bit_alu_3 (
    .Cin(n1_bit_alu_2_cout), .A(A[2]), .B(B[2]), .Output(out_5[2]), .Cout(n1_bit_alu_3_cout), .in_4(Opcode));
  _1_bit_ALU u_1_bit_alu_4 (
    .Cin(n1_bit_alu_3_cout), .A(A[3]), .B(B[3]), .Output(out_5[3]), .Cout(n1_bit_alu_4_cout), .in_4(Opcode));
  _1_bit_ALU u_1_bit_alu_5 (
    .Cin(n1_bit_alu_4_cout), .A(A[4]), .B(B[4]), .Output(out_5[4]), .Cout(n1_bit_alu_5_cout), .in_4(Opcode));
  _1_bit_ALU u_1_bit_alu_6 (
    .Cin(n1_bit_alu_5_cout), .A(A[5]), .B(B[5]), .Output(out_5[5]), .Cout(n1_bit_alu_6_cout), .in_4(Opcode));
  _1_bit_ALU u_1_bit_alu_7 (
    .Cin(n1_bit_alu_6_cout), .A(A[6]), .B(B[6]), .Output(out_5[6]), .Cout(n1_bit_alu_7_cout), .in_4(Opcode));
  _1_bit_ALU u_1_bit_alu_8 (.Cin(n1_bit_alu_7_cout), .A(A[7]), .B(B[7]), .Output(out_5[7]), .Cout(Cout), .in_4(Opcode));

  // Notes on the sheet:
  //   1
  //   2
  //   3
  //   4
  //   5
  //   6
  //   7
  //   8
  //   Output
endmodule
